# Fritzing sketch D+C (saved by Fritzing 0.9.0b)
breadboards: 1

parts:
  JP1 = USB_MICROB_PLUG [package=micro-b-ra-smt]
  CONN2 = USB connector [package=THT]
  J1 = Power Jack [package=power_jack_pth_lock]

nets:
  VCC: JP1.VCC, CONN2.5V, J1.PWR
  N1: JP1.D-, CONN2.d+
  N2: JP1.D+, CONN2.d-
  GND: JP1.GND, CONN2.GND, CONN2.chassis5, CONN2.chassis6, J1.GND
